// Logisim project BB_V0.1.circ as structural Verilog: 17 circuits, main circuit main
module main (
  input  LD_prime,
  input  [3:0] SW_add,
  input  CLR_prime,
  input  [7:0] SW_data,
  input  ld,
  input  in_6,
  input  CLR,
  input  in_8,
  input  RO,
  input  in_10,
  input  P_R_prime,
  input  Clear,
  input  CE,
  input  CO,
  input  Load,
  input  in_16,
  input  in_17,
  input  in_18,
  input  in_19,
  input  in_20,
  input  in_21,
  input  in_22,
  input  in_23,
  input  [7:0] in_24,
  input  DEBUG,
  output out_26,
  output out_27,
  output out_28,
  output out_29,
  output out_30,
  output out_31,
  output out_32,
  output out_33,
  output [3:0] BUS_Add,
  output [7:0] out_35,
  output out_36,
  output out_37,
  output out_38,
  output out_39
);

  wire A0Q, A1Q, A2Q, A3Q, A4Q, A5Q, A6Q, A7Q, alu_1_out_19, alu_1_out_21, alu_1_out_23, alu_1_out_25,
       alu_1_out_27, alu_1_out_29, alu_1_out_31, alu_1_out_33, and_1_out, B0Q, B1Q, B2Q, B3Q, B4Q, B5Q, B6Q,
       B7Q, CLK, not_1_out, pwr_out, ram_module_1_program, ram_module_1_run, wr_prime_out;
  wire [3:0] ram_1_data_3, ram_1_data_5;
  wire [6:0] ram_1_data_2, ram_1_data_4;
  wire [7:0] n8_bit_register_1_out_19, ram_1_data;

  Clock clock_1 (.out(CLK));
  A_register a_register_1 (
    .LOAD_prime(in_6), .out_22(A7Q), ._3Q(A5Q), ._4Q(A4Q), ._5Q(A3Q), ._6Q(A2Q), ._7Q(A1Q), ._8Q_2(A0Q),
    ._8Q(in_10), .out_13(out_26), .out_14(out_27), .out_15(out_28), .out_16(out_29), .out_17(out_30),
    .out_18(out_31), .out_19(out_32), .out_20(out_33), .in_3(out_26), .in_4(out_27), .in_5(out_28),
    .in_6(out_29), .in_7(out_30), .in_8(out_31), .in_9(out_32), .in_10(out_33), .in_1(CLK), .in_12(in_8),
    .out_21(A6Q));
  B_register b_register_1 (
    .in_1(CLK), .LOAD_prime(in_16), .in_3(out_26), .in_4(out_27), .in_5(out_28), .in_6(out_29),
    .in_7(out_30), .in_8(out_31), .in_9(out_32), .in_10(out_33), .out_13(out_26), .out_14(out_27),
    .out_15(out_28), .out_16(out_29), .out_17(out_30), .out_18(out_31), .out_19(out_32), .out_20(out_33),
    ._1Q(B7Q), ._2Q(B6Q), ._3Q(B5Q), ._4Q(B4Q), ._5Q(B3Q), ._6Q(B2Q), ._7Q(B1Q), ._8Q_2(B0Q), ._8Q(in_18),
    .in_12(in_17));
  ALU alu_1 (
    .in_9(in_21), .in_10(in_23), .out_19(alu_1_out_19), .out_20(out_26), .out_21(alu_1_out_21),
    .out_22(out_27), .out_23(alu_1_out_23), .out_24(out_28), .out_25(alu_1_out_25), .out_26(out_29),
    .out_27(alu_1_out_27), .out_28(out_30), .out_29(alu_1_out_29), .out_30(out_31), .out_31(alu_1_out_31),
    .out_32(out_32), .out_33(alu_1_out_33), .out_34(out_33), .in_1(A7Q), .in_2(A6Q), .in_3(A5Q), .in_4(A4Q),
    .in_5(A3Q), .in_6(A2Q), .in_7(A1Q), .in_8(A0Q), .in_11(B7Q), .in_12(B6Q), .in_13(B5Q), .in_14(B4Q),
    .in_15(B3Q), .in_16(B2Q), .in_17(B1Q), .in_18(B0Q));
  LED led_1 (.in(A6Q));
  LED led_2 (.in(A7Q));
  LED led_3 (.in(A5Q));
  LED led_4 (.in(A4Q));
  LED led_5 (.in(B4Q));
  LED led_6 (.in(B6Q));
  LED led_7 (.in(B7Q));
  LED led_8 (.in(B5Q));
  LED led_9 (.in(A2Q));
  LED led_10 (.in(A0Q));
  LED led_11 (.in(A1Q));
  LED led_12 (.in(A3Q));
  LED led_13 (.in(B0Q));
  LED led_14 (.in(B2Q));
  LED led_15 (.in(B1Q));
  LED led_16 (.in(B3Q));
  LED led_17 (.in(alu_1_out_21));
  LED led_18 (.in(alu_1_out_23));
  LED led_19 (.in(alu_1_out_19));
  LED led_20 (.in(alu_1_out_31));
  LED led_21 (.in(alu_1_out_27));
  LED led_22 (.in(alu_1_out_29));
  LED led_23 (.in(alu_1_out_25));
  LED led_24 (.in(alu_1_out_33));
  assign {out_26, out_27, out_28, out_29, out_30, out_31, out_32, out_33} = DEBUG ? in_24 : 8'bz;  // Controlled_Buffer controlled_buffer_1
  and and_1 (and_1_out, CLK, in_19);
  _8_BIT_REGISTER u_8_bit_register_1 (
    .LOAD_prime(in_20), ._1D(out_26), ._2D(out_28), ._3D(out_30), ._4D(out_32), ._5D(out_27), ._6D(out_29),
    ._7D(out_31), ._8D(out_33), .out_12(n8_bit_register_1_out_19[7]), .out_13(n8_bit_register_1_out_19[6]),
    .out_16(n8_bit_register_1_out_19[3]), .out_17(n8_bit_register_1_out_19[2]),
    .out_18(n8_bit_register_1_out_19[1]), .out_19(n8_bit_register_1_out_19[0]), .in_11(in_22),
    .out_15(n8_bit_register_1_out_19[4]), .out_14(n8_bit_register_1_out_19[5]), .in_1(and_1_out));
  _4_bit_register u_4_bit_register_1 (
    .in_1(CLK), .LOAD_prime(LD_prime), .in_4(CLR_prime), .in_3({out_30, out_31, out_32, out_33}),
    .out_5(BUS_Add));
  LED led_25 (.in(ram_module_1_run));
  LED led_26 (.in(ram_module_1_program));
  not not_1 (not_1_out, wr_prime_out);
  Button wr_prime (.out(wr_prime_out));
  Button pwr (.out(pwr_out));
  _7_Segment_Display u_7_segment_display_1 (
    .g(ram_1_data_4[0]), .f(ram_1_data_4[1]), .a(ram_1_data_4[6]), .b(ram_1_data_4[5]), .e(ram_1_data_5[0]),
    .d(ram_1_data_5[1]), .c(ram_1_data_5[2]), .dp(ram_1_data_5[3]));
  Ram_module ram_module_1 (
    .BUS_data({out_26, out_27, out_28, out_29, out_30, out_31, out_32, out_33}), .SW_data(SW_data),
    .BUS_add(BUS_Add), .SW_add(SW_add), .in_5(P_R_prime), .CLK(CLK), .WR_prime(not_1_out), .pwr(pwr_out),
    .out_12(out_35), .run(ram_module_1_run),
    .out_14({out_26, out_27, out_28, out_29, out_30, out_31, out_32, out_33}),
    .Program(ram_module_1_program), .R0(ld), .Clear(CLR), .R0_2(RO));
  PC pc_1 (
    .Clear(Clear), .CE(CE), .CO(CO), .Load(Load), .out_10(out_26), .out_11(out_27), .out_12(out_28),
    .out_13(out_29), .D0(out_33), .D1(out_32), .D2(out_31), .D3(out_30), .out_18(out_36), .out_19(out_37),
    .out_20(out_38), .out_21(out_39), .CLK(CLK), .in_3(out_33), .in_4(out_32), .in_5(out_31), .in_6(out_30));
  _7_Segment_Display u_7_segment_display_2 (
    .g(ram_1_data_2[0]), .f(ram_1_data_2[1]), .a(ram_1_data_2[6]), .b(ram_1_data_2[5]), .e(ram_1_data_3[0]),
    .d(ram_1_data_3[1]), .c(ram_1_data_3[2]), .dp(ram_1_data_3[3]));
  RAM #(.dataWidth(24), .bus("asynch")) ram_1 (
    .addr(n8_bit_register_1_out_19),
    .data({ram_1_data_5[3], ram_1_data_4[6:5], ram_1_data_5[2:0], ram_1_data_4[1:0], ram_1_data_3[3], ram_1_data_2[6:5], ram_1_data_3[2:0], ram_1_data_2[1:0], ram_1_data}));  // open: sel, ld, clr
  _7_Segment_Display u_7_segment_display_3 (
    .g(ram_1_data[0]), .f(ram_1_data[1]), .a(ram_1_data[6]), .b(ram_1_data[5]), .e(ram_1_data[2]),
    .d(ram_1_data[3]), .c(ram_1_data[4]), .dp(ram_1_data[7]));

  // Other names for the same wires on the sheet: B0 = out_33; B1 = out_32; B2 = out_31; B3 = out_30; B4 = out_29;
  //   B5 = out_28; B6 = out_27; B7 = out_26
endmodule

module Clock_Module (
  input  HLT,
  output CLK
);

  wire clock_1_out, not_1_out;

  Clock clock_1 (.out(clock_1_out));
  not not_1 (not_1_out, HLT);
  and and_1 (CLK, clock_1_out, not_1_out);

  // Notes on the sheet:
  //   Clock Module
endmodule

module D_FLIPFLOP (
  input  in_1,
  input  CLK,
  input  D,
  output Q
);

  wire and_1_out, and_2_out, and_3_out, nor_2_out, not_1_out, not_2_out, not_3_out, not_4_out, not_5_out;

  not not_1 (not_1_out, not_2_out);
  not not_2 (not_2_out, CLK);
  not not_3 (not_3_out, not_1_out);
  and and_1 (and_1_out, CLK, not_3_out);
  not not_4 (not_4_out, D);
  not not_5 (not_5_out, in_1);
  and and_2 (and_2_out, not_4_out, and_1_out);
  and and_3 (and_3_out, and_1_out, D);
  nor nor_1 (Q, not_5_out, and_2_out, nor_2_out);
  nor nor_2 (nor_2_out, Q, and_3_out);

  // Notes on the sheet:
  //   S
  //   Q
endmodule

module D_FF_WITH_LOAD (
  input  in_1,
  input  in_2,
  input  in_3,
  input  in_4,
  output out_5
);

  wire and_1_out, and_2_out, not_1_out, or_1_out;

  and and_1 (and_1_out, out_5, in_2);
  not not_1 (not_1_out, in_2);
  and and_2 (and_2_out, not_1_out, in_3);
  or or_1 (or_1_out, and_1_out, and_2_out);
  D_FLIPFLOP d_flipflop_1 (.CLK(in_1), .D(or_1_out), .Q(out_5), .in_1(in_4));
endmodule

module _8_BIT_REGISTER (
  input  in_1,
  input  LOAD_prime,
  input  _1D,
  input  _2D,
  input  _3D,
  input  _4D,
  input  _5D,
  input  _6D,
  input  _7D,
  input  _8D,
  input  in_11,
  output out_12,
  output out_13,
  output out_14,
  output out_15,
  output out_16,
  output out_17,
  output out_18,
  output out_19
);

  Pull_Resistor #(.pull(1)) pull_resistor_1 (.node(_1D));
  D_FF_WITH_LOAD d_ff_with_load_1 (.in_1(in_1), .in_3(_1D), .in_4(in_11), .in_2(LOAD_prime), .out_5(out_12));
  Pull_Resistor #(.pull(1)) pull_resistor_2 (.node(_2D));
  D_FF_WITH_LOAD d_ff_with_load_2 (.in_1(in_1), .in_3(_2D), .in_4(in_11), .in_2(LOAD_prime), .out_5(out_13));
  D_FF_WITH_LOAD d_ff_with_load_3 (.in_1(in_1), .in_3(_3D), .in_4(in_11), .in_2(LOAD_prime), .out_5(out_14));
  Pull_Resistor #(.pull(1)) pull_resistor_3 (.node(_3D));
  Pull_Resistor #(.pull(1)) pull_resistor_4 (.node(_4D));
  D_FF_WITH_LOAD d_ff_with_load_4 (.in_1(in_1), .in_3(_4D), .in_4(in_11), .in_2(LOAD_prime), .out_5(out_15));
  Pull_Resistor #(.pull(1)) pull_resistor_5 (.node(_5D));
  D_FF_WITH_LOAD d_ff_with_load_5 (.in_1(in_1), .in_3(_5D), .in_4(in_11), .in_2(LOAD_prime), .out_5(out_16));
  Pull_Resistor #(.pull(1)) pull_resistor_6 (.node(_6D));
  D_FF_WITH_LOAD d_ff_with_load_6 (.in_1(in_1), .in_3(_6D), .in_4(in_11), .in_2(LOAD_prime), .out_5(out_17));
  Pull_Resistor #(.pull(1)) pull_resistor_7 (.node(_7D));
  D_FF_WITH_LOAD d_ff_with_load_7 (.in_1(in_1), .in_3(_7D), .in_4(in_11), .in_2(LOAD_prime), .out_5(out_18));
  Pull_Resistor #(.pull(1)) pull_resistor_8 (.node(_8D));
  D_FF_WITH_LOAD d_ff_with_load_8 (.in_1(in_1), .in_3(_8D), .in_4(in_11), .in_2(LOAD_prime), .out_5(out_19));
endmodule

module A_register (
  input  in_1,
  input  LOAD_prime,
  input  in_3,
  input  in_4,
  input  in_5,
  input  in_6,
  input  in_7,
  input  in_8,
  input  in_9,
  input  in_10,
  input  _8Q,
  input  in_12,
  output out_13,
  output out_14,
  output out_15,
  output out_16,
  output out_17,
  output out_18,
  output out_19,
  output out_20,
  output out_21,
  output out_22,
  output _3Q,
  output _4Q,
  output _5Q,
  output _6Q,
  output _7Q,
  output _8Q_2
);

  wire not_1_out;

  _8_BIT_REGISTER u_8_bit_register_1 (
    .LOAD_prime(LOAD_prime), ._1D(in_3), ._2D(in_4), ._3D(in_5), ._4D(in_6), ._5D(in_7), ._6D(in_8),
    ._7D(in_9), ._8D(in_10), .out_12(out_21), .out_13(out_22), .out_16(_5Q), .out_17(_6Q), .out_18(_7Q),
    .out_19(_8Q_2), .in_11(in_12), .out_15(_4Q), .out_14(_3Q), .in_1(in_1));
  assign out_13 = not_1_out ? out_21 : 1'bz;  // Controlled_Buffer controlled_buffer_1
  assign out_14 = not_1_out ? out_22 : 1'bz;  // Controlled_Buffer controlled_buffer_2
  assign out_15 = not_1_out ? _3Q : 1'bz;  // Controlled_Buffer controlled_buffer_3
  assign out_16 = not_1_out ? _4Q : 1'bz;  // Controlled_Buffer controlled_buffer_4
  assign out_17 = not_1_out ? _5Q : 1'bz;  // Controlled_Buffer controlled_buffer_5
  assign out_18 = not_1_out ? _6Q : 1'bz;  // Controlled_Buffer controlled_buffer_6
  assign out_19 = not_1_out ? _7Q : 1'bz;  // Controlled_Buffer controlled_buffer_7
  assign out_20 = not_1_out ? _8Q_2 : 1'bz;  // Controlled_Buffer controlled_buffer_8
  not not_1 (not_1_out, _8Q);
endmodule

module B_register (
  input  in_1,
  input  LOAD_prime,
  input  in_3,
  input  in_4,
  input  in_5,
  input  in_6,
  input  in_7,
  input  in_8,
  input  in_9,
  input  in_10,
  input  _8Q,
  input  in_12,
  output out_13,
  output out_14,
  output out_15,
  output out_16,
  output out_17,
  output out_18,
  output out_19,
  output out_20,
  output _1Q,
  output _2Q,
  output _3Q,
  output _4Q,
  output _5Q,
  output _6Q,
  output _7Q,
  output _8Q_2
);

  wire not_1_out;

  _8_BIT_REGISTER u_8_bit_register_1 (
    .LOAD_prime(LOAD_prime), ._1D(in_3), ._2D(in_4), ._3D(in_5), ._4D(in_6), ._5D(in_7), ._6D(in_8),
    ._7D(in_9), ._8D(in_10), .out_12(_1Q), .out_13(_2Q), .out_16(_5Q), .out_17(_6Q), .out_18(_7Q),
    .out_19(_8Q_2), .in_11(in_12), .out_15(_4Q), .out_14(_3Q), .in_1(in_1));
  assign out_13 = not_1_out ? _1Q : 1'bz;  // Controlled_Buffer controlled_buffer_1
  assign out_14 = not_1_out ? _2Q : 1'bz;  // Controlled_Buffer controlled_buffer_2
  assign out_15 = not_1_out ? _3Q : 1'bz;  // Controlled_Buffer controlled_buffer_3
  assign out_16 = not_1_out ? _4Q : 1'bz;  // Controlled_Buffer controlled_buffer_4
  assign out_17 = not_1_out ? _5Q : 1'bz;  // Controlled_Buffer controlled_buffer_5
  assign out_18 = not_1_out ? _6Q : 1'bz;  // Controlled_Buffer controlled_buffer_6
  assign out_19 = not_1_out ? _7Q : 1'bz;  // Controlled_Buffer controlled_buffer_7
  assign out_20 = not_1_out ? _8Q_2 : 1'bz;  // Controlled_Buffer controlled_buffer_8
  not not_1 (not_1_out, _8Q);
endmodule

module Fast_Carry_Adder (
  input  A,
  input  B,
  input  Cin,
  output pi,
  output Gi,
  output S
);

  and and_1 (pi, A, B);
  xor xor_1 (Gi, B, A);
  xor xor_2 (S, Cin, Gi);
endmodule

module _8_bit_fast_carry_adder (
  input  in_1,
  input  in_2,
  input  in_3,
  input  in_4,
  input  in_5,
  input  in_6,
  input  in_7,
  input  in_8,
  input  in_9,
  input  in_10,
  output out_11,
  output out_12,
  output out_13,
  output out_14,
  output out_15,
  output out_16,
  output out_17,
  output out_18,
  output out_19
);

  wire and_1_out, and_2_out, and_3_out, and_4_out, and_5_out, and_6_out, and_7_out, C1, C2, C3, G0, G1, G2,
       G3, P0, P1, P2, P3;

  Fast_Carry_Adder fast_carry_adder_1 (.A(in_1), .B(in_7), .Cin(in_6), .S(out_16), .Gi(P0), .pi(G0));
  and and_1 (and_1_out, P0, in_6);
  xor xor_1 (C1, G0, and_1_out);
  Fast_Carry_Adder fast_carry_adder_2 (.A(in_2), .B(in_8), .Cin(C1), .S(out_17), .Gi(P1), .pi(G1));
  and and_2 (and_2_out, P1, C1);
  xor xor_2 (C2, G1, and_2_out);
  Fast_Carry_Adder fast_carry_adder_3 (.A(in_3), .B(in_9), .Cin(C2), .S(out_18), .Gi(P2), .pi(G2));
  and and_3 (and_3_out, P2, G1);
  ExactlyOne xor_3 (.out(C3), .in0(G2), .in1(and_3_out), .in2(and_4_out));
  and and_4 (and_4_out, P2, P1, C1);
  Fast_Carry_Adder fast_carry_adder_4 (.A(in_4), .B(in_10), .Cin(C3), .S(out_19), .Gi(P3), .pi(G3));
  and and_5 (and_5_out, P3, G2);
  ExactlyOne xor_4 (.out(out_11), .in0(G3), .in1(and_5_out), .in2(and_6_out), .in3(and_7_out));
  and and_6 (and_6_out, P2, P3, G1);
  assign out_12 = in_5 ? out_19 : 1'bz;  // Controlled_Buffer controlled_buffer_1
  assign out_13 = in_5 ? out_18 : 1'bz;  // Controlled_Buffer controlled_buffer_2
  assign out_14 = in_5 ? out_17 : 1'bz;  // Controlled_Buffer controlled_buffer_3
  assign out_15 = in_5 ? out_16 : 1'bz;  // Controlled_Buffer controlled_buffer_4
  and and_7 (and_7_out, P1, P2, P3, C1);

  // Other names for the same wires on the sheet: A0 = in_1; A1 = in_2; A2 = in_3; A3 = in_4; B0 = in_7; B1 = in_8;
  //   B2 = in_9; B3 = in_10; Cin = in_6; CO = out_11; S0 = out_16; S1 = out_17; S2 = out_18; S3 = out_19
endmodule

module ALU (
  input  in_1,
  input  in_2,
  input  in_3,
  input  in_4,
  input  in_5,
  input  in_6,
  input  in_7,
  input  in_8,
  input  in_9,
  input  in_10,
  input  in_11,
  input  in_12,
  input  in_13,
  input  in_14,
  input  in_15,
  input  in_16,
  input  in_17,
  input  in_18,
  output out_19,
  output out_20,
  output out_21,
  output out_22,
  output out_23,
  output out_24,
  output out_25,
  output out_26,
  output out_27,
  output out_28,
  output out_29,
  output out_30,
  output out_31,
  output out_32,
  output out_33,
  output out_34
);

  wire n8_bit_fast_carry_adder_2_out_11, not_1_out, xor_1_out, xor_2_out, xor_3_out, xor_4_out, xor_5_out,
       xor_6_out, xor_7_out, xor_8_out;

  not not_1 (not_1_out, in_9);
  _8_bit_fast_carry_adder u_8_bit_fast_carry_adder_1 (
    .in_6(n8_bit_fast_carry_adder_2_out_11), .out_12(out_20), .out_13(out_22), .out_14(out_24),
    .out_15(out_26), .in_1(in_4), .in_2(in_3), .in_3(in_2), .in_4(in_1), .in_7(xor_4_out), .in_8(xor_3_out),
    .in_9(xor_1_out), .in_10(xor_2_out), .out_16(out_25), .out_17(out_23), .out_18(out_21), .out_19(out_19),
    .in_5(not_1_out));  // open: out_11
  xor xor_1 (xor_1_out, in_10, in_12);
  xor xor_2 (xor_2_out, in_10, in_11);
  xor xor_3 (xor_3_out, in_10, in_13);
  xor xor_4 (xor_4_out, in_10, in_14);
  _8_bit_fast_carry_adder u_8_bit_fast_carry_adder_2 (
    .in_6(in_10), .out_11(n8_bit_fast_carry_adder_2_out_11), .out_12(out_28), .out_13(out_30),
    .out_14(out_32), .out_15(out_34), .in_1(in_8), .in_2(in_7), .in_3(in_6), .in_4(in_5), .in_7(xor_8_out),
    .in_8(xor_7_out), .in_9(xor_6_out), .in_10(xor_5_out), .out_16(out_33), .out_17(out_31), .out_18(out_29),
    .out_19(out_27), .in_5(not_1_out));
  xor xor_5 (xor_5_out, in_10, in_15);
  xor xor_6 (xor_6_out, in_10, in_16);
  xor xor_7 (xor_7_out, in_10, in_17);
  xor xor_8 (xor_8_out, in_10, in_18);

  // Other names for the same wires on the sheet: BY0 = out_34; BY1 = out_32; BY2 = out_30; BY3 = out_28; BY4 = out_26;
  //   BY5 = out_24; BY6 = out_22; BY7 = out_20; Y0 = out_33; Y1 = out_31; Y2 = out_29; Y3 = out_27; Y4 = out_25;
  //   Y5 = out_23; Y6 = out_21; Y7 = out_19
endmodule

module SRAM (
  input  in_1,
  input  in_2,
  input  in_3,
  input  in_4,
  input  in_5,
  input  in_6,
  input  in_7,
  input  in_8,
  input  in_9,
  input  in_10,
  input  in_11,
  input  in_12,
  input  in_13,
  input  in_14,
  input  in_15,
  output out_16,
  output out_17,
  output out_18,
  output out_19,
  output out_20,
  output out_21,
  output out_22,
  output out_23
);

  wire _1Q, _2Q, _3Q, _4Q, _5Q, _6Q, _7Q, _8Q, A0_prime, A1_prime, A2_prime, A3_prime, and_2_out, and_3_out,
       and_4_out, and_5_out, and_6_out, and_7_out, and_8_out, and_9_out, and_10_out, and_11_out, and_12_out,
       and_13_out, and_14_out, and_15_out, and_16_out, and_17_out, and_18_out, CLK, n8_bit_register_1_out_12,
       n8_bit_register_1_out_13, n8_bit_register_1_out_14, n8_bit_register_1_out_15,
       n8_bit_register_1_out_16, n8_bit_register_1_out_17, n8_bit_register_1_out_18,
       n8_bit_register_1_out_19, n8_bit_register_2_out_12, n8_bit_register_2_out_13,
       n8_bit_register_2_out_14, n8_bit_register_2_out_15, n8_bit_register_2_out_16,
       n8_bit_register_2_out_17, n8_bit_register_2_out_18, n8_bit_register_2_out_19,
       n8_bit_register_3_out_12, n8_bit_register_3_out_13, n8_bit_register_3_out_14,
       n8_bit_register_3_out_15, n8_bit_register_3_out_16, n8_bit_register_3_out_17,
       n8_bit_register_3_out_18, n8_bit_register_3_out_19, n8_bit_register_4_out_12,
       n8_bit_register_4_out_13, n8_bit_register_4_out_14, n8_bit_register_4_out_15,
       n8_bit_register_4_out_16, n8_bit_register_4_out_17, n8_bit_register_4_out_18,
       n8_bit_register_4_out_19, n8_bit_register_5_out_12, n8_bit_register_5_out_13,
       n8_bit_register_5_out_14, n8_bit_register_5_out_15, n8_bit_register_5_out_16,
       n8_bit_register_5_out_17, n8_bit_register_5_out_18, n8_bit_register_5_out_19,
       n8_bit_register_6_out_12, n8_bit_register_6_out_13, n8_bit_register_6_out_14,
       n8_bit_register_6_out_15, n8_bit_register_6_out_16, n8_bit_register_6_out_17,
       n8_bit_register_6_out_18, n8_bit_register_6_out_19, n8_bit_register_7_out_12,
       n8_bit_register_7_out_13, n8_bit_register_7_out_14, n8_bit_register_7_out_15,
       n8_bit_register_7_out_16, n8_bit_register_7_out_17, n8_bit_register_7_out_18,
       n8_bit_register_7_out_19, n8_bit_register_8_out_12, n8_bit_register_8_out_13,
       n8_bit_register_8_out_14, n8_bit_register_8_out_15, n8_bit_register_8_out_16,
       n8_bit_register_8_out_17, n8_bit_register_8_out_18, n8_bit_register_8_out_19,
       n8_bit_register_9_out_12, n8_bit_register_9_out_13, n8_bit_register_9_out_14,
       n8_bit_register_9_out_15, n8_bit_register_9_out_16, n8_bit_register_9_out_17,
       n8_bit_register_9_out_18, n8_bit_register_9_out_19, n8_bit_register_10_out_12,
       n8_bit_register_10_out_13, n8_bit_register_10_out_14, n8_bit_register_10_out_15,
       n8_bit_register_10_out_16, n8_bit_register_10_out_17, n8_bit_register_10_out_18,
       n8_bit_register_10_out_19, n8_bit_register_11_out_12, n8_bit_register_11_out_13,
       n8_bit_register_11_out_14, n8_bit_register_11_out_15, n8_bit_register_11_out_16,
       n8_bit_register_11_out_17, n8_bit_register_11_out_18, n8_bit_register_11_out_19,
       n8_bit_register_12_out_12, n8_bit_register_12_out_13, n8_bit_register_12_out_14,
       n8_bit_register_12_out_15, n8_bit_register_12_out_16, n8_bit_register_12_out_17,
       n8_bit_register_12_out_18, n8_bit_register_12_out_19, n8_bit_register_13_out_12,
       n8_bit_register_13_out_13, n8_bit_register_13_out_14, n8_bit_register_13_out_15,
       n8_bit_register_13_out_16, n8_bit_register_13_out_17, n8_bit_register_13_out_18,
       n8_bit_register_13_out_19, n8_bit_register_14_out_12, n8_bit_register_14_out_13,
       n8_bit_register_14_out_14, n8_bit_register_14_out_15, n8_bit_register_14_out_16,
       n8_bit_register_14_out_17, n8_bit_register_14_out_18, n8_bit_register_14_out_19,
       n8_bit_register_15_out_12, n8_bit_register_15_out_13, n8_bit_register_15_out_14,
       n8_bit_register_15_out_15, n8_bit_register_15_out_16, n8_bit_register_15_out_17,
       n8_bit_register_15_out_18, n8_bit_register_15_out_19, n8_bit_register_16_out_12,
       n8_bit_register_16_out_13, n8_bit_register_16_out_14, n8_bit_register_16_out_15,
       n8_bit_register_16_out_16, n8_bit_register_16_out_17, n8_bit_register_16_out_18,
       n8_bit_register_16_out_19, not_3_out, not_4_out, not_5_out, not_11_out, not_12_out, not_13_out,
       not_14_out, not_15_out, not_16_out, not_17_out, not_18_out, not_19_out, not_20_out, not_21_out,
       not_22_out, not_23_out, not_24_out, not_25_out, not_26_out, not_27_out, not_28_out, not_29_out,
       not_30_out, not_31_out, not_32_out, not_33_out, not_34_out, not_35_out, not_36_out, not_37_out,
       not_38_out, not_39_out, or_14_out, or_15_out, or_16_out, or_17_out, or_18_out, or_19_out, or_20_out,
       or_21_out, or_22_out, or_23_out, or_24_out, or_25_out, or_26_out, or_27_out, or_28_out, or_29_out, S0,
       S1, S2, S3, S4, S5, S6, S7, S8, S9, S10, S11, S12, S13, S14, S15, undriven;

  not not_1 (A3_prime, in_1);
  not not_2 (A1_prime, in_5);
  not not_3 (not_3_out, in_3);
  not not_4 (not_4_out, in_4);
  not not_5 (not_5_out, in_3);
  and and_1 (CLK, not_3_out, not_4_out);
  assign out_16 = and_2_out ? _1Q : 1'bz;  // Controlled_Buffer controlled_buffer_1
  assign out_17 = and_2_out ? _2Q : 1'bz;  // Controlled_Buffer controlled_buffer_2
  assign out_18 = and_2_out ? _3Q : 1'bz;  // Controlled_Buffer controlled_buffer_3
  assign out_19 = and_2_out ? _4Q : 1'bz;  // Controlled_Buffer controlled_buffer_4
  assign out_20 = and_2_out ? _5Q : 1'bz;  // Controlled_Buffer controlled_buffer_5
  assign out_21 = and_2_out ? _6Q : 1'bz;  // Controlled_Buffer controlled_buffer_6
  assign out_22 = and_2_out ? _7Q : 1'bz;  // Controlled_Buffer controlled_buffer_7
  assign out_23 = and_2_out ? _8Q : 1'bz;  // Controlled_Buffer controlled_buffer_8
  and and_2 (and_2_out, not_5_out, in_4);
  and and_3 (and_3_out, A3_prime, A2_prime, A1_prime, A0_prime);
  and and_4 (and_4_out, A3_prime, A2_prime, A1_prime, in_6);
  and and_5 (and_5_out, A3_prime, A2_prime, in_5, A0_prime);
  and and_6 (and_6_out, A3_prime, A2_prime, in_5, in_6);
  and and_7 (and_7_out, A3_prime, in_2, A1_prime, A0_prime);
  and and_8 (and_8_out, A3_prime, in_2, A1_prime, in_6);
  and and_9 (and_9_out, A3_prime, in_2, in_5, A0_prime);
  and and_10 (and_10_out, A3_prime, in_2, in_5, in_6);
  not not_6 (A2_prime, in_2);
  not not_7 (A0_prime, in_6);
  not not_8 (S0, and_3_out);
  not not_9 (S1, and_4_out);
  not not_10 (S2, and_5_out);
  not not_11 (not_11_out, and_6_out);
  or or_1 (S3, not_11_out, CLK);
  not not_12 (not_12_out, and_7_out);
  or or_2 (S4, not_12_out, CLK);
  not not_13 (not_13_out, and_8_out);
  or or_3 (S5, not_13_out, CLK);
  not not_14 (not_14_out, and_9_out);
  or or_4 (S6, not_14_out, CLK);
  not not_15 (not_15_out, and_10_out);
  or or_5 (S7, not_15_out, CLK);
  and and_11 (and_11_out, in_1, A2_prime, A1_prime, A0_prime);
  not not_16 (not_16_out, and_11_out);
  and and_12 (and_12_out, in_1, A2_prime, A1_prime, in_6);
  not not_17 (not_17_out, and_12_out);
  and and_13 (and_13_out, in_1, A2_prime, in_5, A0_prime);
  not not_18 (not_18_out, and_13_out);
  and and_14 (and_14_out, in_1, A2_prime, in_5, in_6);
  not not_19 (not_19_out, and_14_out);
  not not_20 (not_20_out, and_15_out);
  and and_15 (and_15_out, in_1, in_2, A1_prime, A0_prime);
  not not_21 (not_21_out, and_16_out);
  and and_16 (and_16_out, in_1, in_2, A1_prime, in_6);
  not not_22 (not_22_out, and_17_out);
  and and_17 (and_17_out, in_1, in_2, in_5, A0_prime);
  and and_18 (and_18_out, in_1, in_2, in_5, in_6);
  not not_23 (not_23_out, and_18_out);
  or or_6 (S8, not_16_out, CLK);
  or or_7 (S9, not_17_out, CLK);
  or or_8 (S10, not_18_out, CLK);
  or or_9 (S11, not_19_out, CLK);
  or or_10 (S12, not_20_out, CLK);
  or or_11 (S13, not_21_out, CLK);
  or or_12 (S14, not_22_out, CLK);
  or or_13 (S15, not_23_out, undriven);
  _8_BIT_REGISTER u_8_bit_register_1 (
    .LOAD_prime(CLK), ._1D(in_8), ._2D(in_9), ._3D(in_10), ._4D(in_11), ._5D(in_12), ._6D(in_13),
    ._7D(in_14), ._8D(in_15), .out_12(n8_bit_register_1_out_12), .out_13(n8_bit_register_1_out_13),
    .out_16(n8_bit_register_1_out_16), .out_17(n8_bit_register_1_out_17), .out_18(n8_bit_register_1_out_18),
    .out_19(n8_bit_register_1_out_19), .in_11(or_14_out), .out_15(n8_bit_register_1_out_15),
    .out_14(n8_bit_register_1_out_14), .in_1(CLK));
  _8_BIT_REGISTER u_8_bit_register_2 (
    .LOAD_prime(S4), ._1D(in_8), ._2D(in_9), ._3D(in_10), ._4D(in_11), ._5D(in_12), ._6D(in_13), ._7D(in_14),
    ._8D(in_15), .out_12(n8_bit_register_2_out_12), .out_13(n8_bit_register_2_out_13),
    .out_16(n8_bit_register_2_out_16), .out_17(n8_bit_register_2_out_17), .out_18(n8_bit_register_2_out_18),
    .out_19(n8_bit_register_2_out_19), .in_11(or_15_out), .out_15(n8_bit_register_2_out_15),
    .out_14(n8_bit_register_2_out_14), .in_1(CLK));
  _8_BIT_REGISTER u_8_bit_register_3 (
    .LOAD_prime(S8), ._1D(in_8), ._2D(in_9), ._3D(in_10), ._4D(in_11), ._5D(in_12), ._6D(in_13), ._7D(in_14),
    ._8D(in_15), .out_12(n8_bit_register_3_out_12), .out_13(n8_bit_register_3_out_13),
    .out_16(n8_bit_register_3_out_16), .out_17(n8_bit_register_3_out_17), .out_18(n8_bit_register_3_out_18),
    .out_19(n8_bit_register_3_out_19), .in_11(or_16_out), .out_15(n8_bit_register_3_out_15),
    .out_14(n8_bit_register_3_out_14), .in_1(CLK));
  _8_BIT_REGISTER u_8_bit_register_4 (
    .LOAD_prime(S12), ._1D(in_8), ._2D(in_9), ._3D(in_10), ._4D(in_11), ._5D(in_12), ._6D(in_13),
    ._7D(in_14), ._8D(in_15), .out_12(n8_bit_register_4_out_12), .out_13(n8_bit_register_4_out_13),
    .out_16(n8_bit_register_4_out_16), .out_17(n8_bit_register_4_out_17), .out_18(n8_bit_register_4_out_18),
    .out_19(n8_bit_register_4_out_19), .in_11(or_17_out), .out_15(n8_bit_register_4_out_15),
    .out_14(n8_bit_register_4_out_14), .in_1(CLK));
  assign _1Q = not_24_out ? n8_bit_register_1_out_12 : 1'bz;  // Controlled_Buffer controlled_buffer_9
  assign _2Q = not_24_out ? n8_bit_register_1_out_13 : 1'bz;  // Controlled_Buffer controlled_buffer_10
  assign _3Q = not_24_out ? n8_bit_register_1_out_14 : 1'bz;  // Controlled_Buffer controlled_buffer_11
  assign _4Q = not_24_out ? n8_bit_register_1_out_15 : 1'bz;  // Controlled_Buffer controlled_buffer_12
  assign _5Q = not_24_out ? n8_bit_register_1_out_16 : 1'bz;  // Controlled_Buffer controlled_buffer_13
  assign _6Q = not_24_out ? n8_bit_register_1_out_17 : 1'bz;  // Controlled_Buffer controlled_buffer_14
  assign _7Q = not_24_out ? n8_bit_register_1_out_18 : 1'bz;  // Controlled_Buffer controlled_buffer_15
  assign _8Q = not_24_out ? n8_bit_register_1_out_19 : 1'bz;  // Controlled_Buffer controlled_buffer_16
  not not_24 (not_24_out, S0);
  or or_14 (or_14_out, in_7, S0);
  assign _1Q = not_25_out ? n8_bit_register_2_out_12 : 1'bz;  // Controlled_Buffer controlled_buffer_17
  assign _2Q = not_25_out ? n8_bit_register_2_out_13 : 1'bz;  // Controlled_Buffer controlled_buffer_18
  assign _3Q = not_25_out ? n8_bit_register_2_out_14 : 1'bz;  // Controlled_Buffer controlled_buffer_19
  assign _4Q = not_25_out ? n8_bit_register_2_out_15 : 1'bz;  // Controlled_Buffer controlled_buffer_20
  assign _5Q = not_25_out ? n8_bit_register_2_out_16 : 1'bz;  // Controlled_Buffer controlled_buffer_21
  assign _6Q = not_25_out ? n8_bit_register_2_out_17 : 1'bz;  // Controlled_Buffer controlled_buffer_22
  assign _7Q = not_25_out ? n8_bit_register_2_out_18 : 1'bz;  // Controlled_Buffer controlled_buffer_23
  assign _8Q = not_25_out ? n8_bit_register_2_out_19 : 1'bz;  // Controlled_Buffer controlled_buffer_24
  not not_25 (not_25_out, S4);
  or or_15 (or_15_out, in_7, S4);
  assign _1Q = not_26_out ? n8_bit_register_3_out_12 : 1'bz;  // Controlled_Buffer controlled_buffer_25
  assign _2Q = not_26_out ? n8_bit_register_3_out_13 : 1'bz;  // Controlled_Buffer controlled_buffer_26
  assign _3Q = not_26_out ? n8_bit_register_3_out_14 : 1'bz;  // Controlled_Buffer controlled_buffer_27
  assign _4Q = not_26_out ? n8_bit_register_3_out_15 : 1'bz;  // Controlled_Buffer controlled_buffer_28
  assign _5Q = not_26_out ? n8_bit_register_3_out_16 : 1'bz;  // Controlled_Buffer controlled_buffer_29
  assign _6Q = not_26_out ? n8_bit_register_3_out_17 : 1'bz;  // Controlled_Buffer controlled_buffer_30
  assign _7Q = not_26_out ? n8_bit_register_3_out_18 : 1'bz;  // Controlled_Buffer controlled_buffer_31
  assign _8Q = not_26_out ? n8_bit_register_3_out_19 : 1'bz;  // Controlled_Buffer controlled_buffer_32
  not not_26 (not_26_out, S8);
  or or_16 (or_16_out, in_7, S8);
  assign _1Q = not_27_out ? n8_bit_register_4_out_12 : 1'bz;  // Controlled_Buffer controlled_buffer_33
  assign _2Q = not_27_out ? n8_bit_register_4_out_13 : 1'bz;  // Controlled_Buffer controlled_buffer_34
  assign _3Q = not_27_out ? n8_bit_register_4_out_14 : 1'bz;  // Controlled_Buffer controlled_buffer_35
  assign _4Q = not_27_out ? n8_bit_register_4_out_15 : 1'bz;  // Controlled_Buffer controlled_buffer_36
  assign _5Q = not_27_out ? n8_bit_register_4_out_16 : 1'bz;  // Controlled_Buffer controlled_buffer_37
  assign _6Q = not_27_out ? n8_bit_register_4_out_17 : 1'bz;  // Controlled_Buffer controlled_buffer_38
  assign _7Q = not_27_out ? n8_bit_register_4_out_18 : 1'bz;  // Controlled_Buffer controlled_buffer_39
  assign _8Q = not_27_out ? n8_bit_register_4_out_19 : 1'bz;  // Controlled_Buffer controlled_buffer_40
  not not_27 (not_27_out, S12);
  or or_17 (or_17_out, in_7, S12);
  assign _1Q = not_28_out ? n8_bit_register_5_out_12 : 1'bz;  // Controlled_Buffer controlled_buffer_41
  _8_BIT_REGISTER u_8_bit_register_5 (
    .LOAD_prime(CLK), ._1D(in_8), ._2D(in_9), ._3D(in_10), ._4D(in_11), ._5D(in_12), ._6D(in_13),
    ._7D(in_14), ._8D(in_15), .out_12(n8_bit_register_5_out_12), .out_13(n8_bit_register_5_out_13),
    .out_16(n8_bit_register_5_out_16), .out_17(n8_bit_register_5_out_17), .out_18(n8_bit_register_5_out_18),
    .out_19(n8_bit_register_5_out_19), .in_11(or_18_out), .out_15(n8_bit_register_5_out_15),
    .out_14(n8_bit_register_5_out_14), .in_1(CLK));
  assign _2Q = not_28_out ? n8_bit_register_5_out_13 : 1'bz;  // Controlled_Buffer controlled_buffer_42
  assign _3Q = not_28_out ? n8_bit_register_5_out_14 : 1'bz;  // Controlled_Buffer controlled_buffer_43
  assign _4Q = not_28_out ? n8_bit_register_5_out_15 : 1'bz;  // Controlled_Buffer controlled_buffer_44
  assign _5Q = not_28_out ? n8_bit_register_5_out_16 : 1'bz;  // Controlled_Buffer controlled_buffer_45
  assign _6Q = not_28_out ? n8_bit_register_5_out_17 : 1'bz;  // Controlled_Buffer controlled_buffer_46
  assign _7Q = not_28_out ? n8_bit_register_5_out_18 : 1'bz;  // Controlled_Buffer controlled_buffer_47
  assign _8Q = not_28_out ? n8_bit_register_5_out_19 : 1'bz;  // Controlled_Buffer controlled_buffer_48
  not not_28 (not_28_out, S1);
  or or_18 (or_18_out, in_7, S1);
  assign _1Q = not_29_out ? n8_bit_register_6_out_12 : 1'bz;  // Controlled_Buffer controlled_buffer_49
  _8_BIT_REGISTER u_8_bit_register_6 (
    .LOAD_prime(S5), ._1D(in_8), ._2D(in_9), ._3D(in_10), ._4D(in_11), ._5D(in_12), ._6D(in_13), ._7D(in_14),
    ._8D(in_15), .out_12(n8_bit_register_6_out_12), .out_13(n8_bit_register_6_out_13),
    .out_16(n8_bit_register_6_out_16), .out_17(n8_bit_register_6_out_17), .out_18(n8_bit_register_6_out_18),
    .out_19(n8_bit_register_6_out_19), .in_11(or_19_out), .out_15(n8_bit_register_6_out_15),
    .out_14(n8_bit_register_6_out_14), .in_1(CLK));
  assign _2Q = not_29_out ? n8_bit_register_6_out_13 : 1'bz;  // Controlled_Buffer controlled_buffer_50
  assign _3Q = not_29_out ? n8_bit_register_6_out_14 : 1'bz;  // Controlled_Buffer controlled_buffer_51
  assign _4Q = not_29_out ? n8_bit_register_6_out_15 : 1'bz;  // Controlled_Buffer controlled_buffer_52
  assign _5Q = not_29_out ? n8_bit_register_6_out_16 : 1'bz;  // Controlled_Buffer controlled_buffer_53
  assign _6Q = not_29_out ? n8_bit_register_6_out_17 : 1'bz;  // Controlled_Buffer controlled_buffer_54
  assign _7Q = not_29_out ? n8_bit_register_6_out_18 : 1'bz;  // Controlled_Buffer controlled_buffer_55
  assign _8Q = not_29_out ? n8_bit_register_6_out_19 : 1'bz;  // Controlled_Buffer controlled_buffer_56
  not not_29 (not_29_out, S5);
  or or_19 (or_19_out, in_7, S5);
  assign _1Q = not_30_out ? n8_bit_register_7_out_12 : 1'bz;  // Controlled_Buffer controlled_buffer_57
  _8_BIT_REGISTER u_8_bit_register_7 (
    .LOAD_prime(S9), ._1D(in_8), ._2D(in_9), ._3D(in_10), ._4D(in_11), ._5D(in_12), ._6D(in_13), ._7D(in_14),
    ._8D(in_15), .out_12(n8_bit_register_7_out_12), .out_13(n8_bit_register_7_out_13),
    .out_16(n8_bit_register_7_out_16), .out_17(n8_bit_register_7_out_17), .out_18(n8_bit_register_7_out_18),
    .out_19(n8_bit_register_7_out_19), .in_11(or_20_out), .out_15(n8_bit_register_7_out_15),
    .out_14(n8_bit_register_7_out_14), .in_1(CLK));
  assign _2Q = not_30_out ? n8_bit_register_7_out_13 : 1'bz;  // Controlled_Buffer controlled_buffer_58
  assign _3Q = not_30_out ? n8_bit_register_7_out_14 : 1'bz;  // Controlled_Buffer controlled_buffer_59
  assign _4Q = not_30_out ? n8_bit_register_7_out_15 : 1'bz;  // Controlled_Buffer controlled_buffer_60
  assign _5Q = not_30_out ? n8_bit_register_7_out_16 : 1'bz;  // Controlled_Buffer controlled_buffer_61
  assign _6Q = not_30_out ? n8_bit_register_7_out_17 : 1'bz;  // Controlled_Buffer controlled_buffer_62
  assign _7Q = not_30_out ? n8_bit_register_7_out_18 : 1'bz;  // Controlled_Buffer controlled_buffer_63
  assign _8Q = not_30_out ? n8_bit_register_7_out_19 : 1'bz;  // Controlled_Buffer controlled_buffer_64
  not not_30 (not_30_out, S9);
  or or_20 (or_20_out, in_7, S9);
  _8_BIT_REGISTER u_8_bit_register_8 (
    .LOAD_prime(S13), ._1D(in_8), ._2D(in_9), ._3D(in_10), ._4D(in_11), ._5D(in_12), ._6D(in_13),
    ._7D(in_14), ._8D(in_15), .out_12(n8_bit_register_8_out_12), .out_13(n8_bit_register_8_out_13),
    .out_16(n8_bit_register_8_out_16), .out_17(n8_bit_register_8_out_17), .out_18(n8_bit_register_8_out_18),
    .out_19(n8_bit_register_8_out_19), .in_11(or_21_out), .out_15(n8_bit_register_8_out_15),
    .out_14(n8_bit_register_8_out_14), .in_1(CLK));
  assign _1Q = not_31_out ? n8_bit_register_8_out_12 : 1'bz;  // Controlled_Buffer controlled_buffer_65
  assign _2Q = not_31_out ? n8_bit_register_8_out_13 : 1'bz;  // Controlled_Buffer controlled_buffer_66
  assign _3Q = not_31_out ? n8_bit_register_8_out_14 : 1'bz;  // Controlled_Buffer controlled_buffer_67
  assign _4Q = not_31_out ? n8_bit_register_8_out_15 : 1'bz;  // Controlled_Buffer controlled_buffer_68
  assign _5Q = not_31_out ? n8_bit_register_8_out_16 : 1'bz;  // Controlled_Buffer controlled_buffer_69
  assign _6Q = not_31_out ? n8_bit_register_8_out_17 : 1'bz;  // Controlled_Buffer controlled_buffer_70
  assign _7Q = not_31_out ? n8_bit_register_8_out_18 : 1'bz;  // Controlled_Buffer controlled_buffer_71
  assign _8Q = not_31_out ? n8_bit_register_8_out_19 : 1'bz;  // Controlled_Buffer controlled_buffer_72
  not not_31 (not_31_out, S13);
  or or_21 (or_21_out, in_7, S13);
  _8_BIT_REGISTER u_8_bit_register_9 (
    .LOAD_prime(CLK), ._1D(in_8), ._2D(in_9), ._3D(in_10), ._4D(in_11), ._5D(in_12), ._6D(in_13),
    ._7D(in_14), ._8D(in_15), .out_12(n8_bit_register_9_out_12), .out_13(n8_bit_register_9_out_13),
    .out_16(n8_bit_register_9_out_16), .out_17(n8_bit_register_9_out_17), .out_18(n8_bit_register_9_out_18),
    .out_19(n8_bit_register_9_out_19), .in_11(or_22_out), .out_15(n8_bit_register_9_out_15),
    .out_14(n8_bit_register_9_out_14), .in_1(CLK));
  _8_BIT_REGISTER u_8_bit_register_10 (
    .LOAD_prime(S6), ._1D(in_8), ._2D(in_9), ._3D(in_10), ._4D(in_11), ._5D(in_12), ._6D(in_13), ._7D(in_14),
    ._8D(in_15), .out_12(n8_bit_register_10_out_12), .out_13(n8_bit_register_10_out_13),
    .out_16(n8_bit_register_10_out_16), .out_17(n8_bit_register_10_out_17),
    .out_18(n8_bit_register_10_out_18), .out_19(n8_bit_register_10_out_19), .in_11(or_23_out),
    .out_15(n8_bit_register_10_out_15), .out_14(n8_bit_register_10_out_14), .in_1(CLK));
  _8_BIT_REGISTER u_8_bit_register_11 (
    .LOAD_prime(S10), ._1D(in_8), ._2D(in_9), ._3D(in_10), ._4D(in_11), ._5D(in_12), ._6D(in_13),
    ._7D(in_14), ._8D(in_15), .out_12(n8_bit_register_11_out_12), .out_13(n8_bit_register_11_out_13),
    .out_16(n8_bit_register_11_out_16), .out_17(n8_bit_register_11_out_17),
    .out_18(n8_bit_register_11_out_18), .out_19(n8_bit_register_11_out_19), .in_11(or_24_out),
    .out_15(n8_bit_register_11_out_15), .out_14(n8_bit_register_11_out_14), .in_1(CLK));
  _8_BIT_REGISTER u_8_bit_register_12 (
    .LOAD_prime(S14), ._1D(in_8), ._2D(in_9), ._3D(in_10), ._4D(in_11), ._5D(in_12), ._6D(in_13),
    ._7D(in_14), ._8D(in_15), .out_12(n8_bit_register_12_out_12), .out_13(n8_bit_register_12_out_13),
    .out_16(n8_bit_register_12_out_16), .out_17(n8_bit_register_12_out_17),
    .out_18(n8_bit_register_12_out_18), .out_19(n8_bit_register_12_out_19), .in_11(or_25_out),
    .out_15(n8_bit_register_12_out_15), .out_14(n8_bit_register_12_out_14), .in_1(CLK));
  assign _1Q = not_32_out ? n8_bit_register_9_out_12 : 1'bz;  // Controlled_Buffer controlled_buffer_73
  assign _2Q = not_32_out ? n8_bit_register_9_out_13 : 1'bz;  // Controlled_Buffer controlled_buffer_74
  assign _3Q = not_32_out ? n8_bit_register_9_out_14 : 1'bz;  // Controlled_Buffer controlled_buffer_75
  assign _4Q = not_32_out ? n8_bit_register_9_out_15 : 1'bz;  // Controlled_Buffer controlled_buffer_76
  assign _5Q = not_32_out ? n8_bit_register_9_out_16 : 1'bz;  // Controlled_Buffer controlled_buffer_77
  assign _6Q = not_32_out ? n8_bit_register_9_out_17 : 1'bz;  // Controlled_Buffer controlled_buffer_78
  assign _7Q = not_32_out ? n8_bit_register_9_out_18 : 1'bz;  // Controlled_Buffer controlled_buffer_79
  assign _8Q = not_32_out ? n8_bit_register_9_out_19 : 1'bz;  // Controlled_Buffer controlled_buffer_80
  not not_32 (not_32_out, S2);
  or or_22 (or_22_out, in_7, S2);
  assign _1Q = not_33_out ? n8_bit_register_10_out_12 : 1'bz;  // Controlled_Buffer controlled_buffer_81
  assign _2Q = not_33_out ? n8_bit_register_10_out_13 : 1'bz;  // Controlled_Buffer controlled_buffer_82
  assign _3Q = not_33_out ? n8_bit_register_10_out_14 : 1'bz;  // Controlled_Buffer controlled_buffer_83
  assign _4Q = not_33_out ? n8_bit_register_10_out_15 : 1'bz;  // Controlled_Buffer controlled_buffer_84
  assign _5Q = not_33_out ? n8_bit_register_10_out_16 : 1'bz;  // Controlled_Buffer controlled_buffer_85
  assign _6Q = not_33_out ? n8_bit_register_10_out_17 : 1'bz;  // Controlled_Buffer controlled_buffer_86
  assign _7Q = not_33_out ? n8_bit_register_10_out_18 : 1'bz;  // Controlled_Buffer controlled_buffer_87
  assign _8Q = not_33_out ? n8_bit_register_10_out_19 : 1'bz;  // Controlled_Buffer controlled_buffer_88
  not not_33 (not_33_out, S6);
  or or_23 (or_23_out, in_7, S6);
  assign _1Q = not_34_out ? n8_bit_register_11_out_12 : 1'bz;  // Controlled_Buffer controlled_buffer_89
  assign _2Q = not_34_out ? n8_bit_register_11_out_13 : 1'bz;  // Controlled_Buffer controlled_buffer_90
  assign _3Q = not_34_out ? n8_bit_register_11_out_14 : 1'bz;  // Controlled_Buffer controlled_buffer_91
  assign _4Q = not_34_out ? n8_bit_register_11_out_15 : 1'bz;  // Controlled_Buffer controlled_buffer_92
  assign _5Q = not_34_out ? n8_bit_register_11_out_16 : 1'bz;  // Controlled_Buffer controlled_buffer_93
  assign _6Q = not_34_out ? n8_bit_register_11_out_17 : 1'bz;  // Controlled_Buffer controlled_buffer_94
  assign _7Q = not_34_out ? n8_bit_register_11_out_18 : 1'bz;  // Controlled_Buffer controlled_buffer_95
  assign _8Q = not_34_out ? n8_bit_register_11_out_19 : 1'bz;  // Controlled_Buffer controlled_buffer_96
  not not_34 (not_34_out, S10);
  or or_24 (or_24_out, in_7, S10);
  assign _1Q = not_35_out ? n8_bit_register_12_out_12 : 1'bz;  // Controlled_Buffer controlled_buffer_97
  assign _2Q = not_35_out ? n8_bit_register_12_out_13 : 1'bz;  // Controlled_Buffer controlled_buffer_98
  assign _3Q = not_35_out ? n8_bit_register_12_out_14 : 1'bz;  // Controlled_Buffer controlled_buffer_99
  assign _4Q = not_35_out ? n8_bit_register_12_out_15 : 1'bz;  // Controlled_Buffer controlled_buffer_100
  assign _5Q = not_35_out ? n8_bit_register_12_out_16 : 1'bz;  // Controlled_Buffer controlled_buffer_101
  assign _6Q = not_35_out ? n8_bit_register_12_out_17 : 1'bz;  // Controlled_Buffer controlled_buffer_102
  assign _7Q = not_35_out ? n8_bit_register_12_out_18 : 1'bz;  // Controlled_Buffer controlled_buffer_103
  assign _8Q = not_35_out ? n8_bit_register_12_out_19 : 1'bz;  // Controlled_Buffer controlled_buffer_104
  not not_35 (not_35_out, S14);
  or or_25 (or_25_out, in_7, S14);
  assign _1Q = not_36_out ? n8_bit_register_13_out_12 : 1'bz;  // Controlled_Buffer controlled_buffer_105
  _8_BIT_REGISTER u_8_bit_register_13 (
    .LOAD_prime(S3), ._1D(in_8), ._2D(in_9), ._3D(in_10), ._4D(in_11), ._5D(in_12), ._6D(in_13), ._7D(in_14),
    ._8D(in_15), .out_12(n8_bit_register_13_out_12), .out_13(n8_bit_register_13_out_13),
    .out_16(n8_bit_register_13_out_16), .out_17(n8_bit_register_13_out_17),
    .out_18(n8_bit_register_13_out_18), .out_19(n8_bit_register_13_out_19), .in_11(or_26_out),
    .out_15(n8_bit_register_13_out_15), .out_14(n8_bit_register_13_out_14), .in_1(CLK));
  assign _2Q = not_36_out ? n8_bit_register_13_out_13 : 1'bz;  // Controlled_Buffer controlled_buffer_106
  assign _3Q = not_36_out ? n8_bit_register_13_out_14 : 1'bz;  // Controlled_Buffer controlled_buffer_107
  assign _4Q = not_36_out ? n8_bit_register_13_out_15 : 1'bz;  // Controlled_Buffer controlled_buffer_108
  assign _5Q = not_36_out ? n8_bit_register_13_out_16 : 1'bz;  // Controlled_Buffer controlled_buffer_109
  assign _6Q = not_36_out ? n8_bit_register_13_out_17 : 1'bz;  // Controlled_Buffer controlled_buffer_110
  assign _7Q = not_36_out ? n8_bit_register_13_out_18 : 1'bz;  // Controlled_Buffer controlled_buffer_111
  assign _8Q = not_36_out ? n8_bit_register_13_out_19 : 1'bz;  // Controlled_Buffer controlled_buffer_112
  not not_36 (not_36_out, S3);
  or or_26 (or_26_out, in_7, S3);
  _8_BIT_REGISTER u_8_bit_register_14 (
    .LOAD_prime(S7), ._1D(in_8), ._2D(in_9), ._3D(in_10), ._4D(in_11), ._5D(in_12), ._6D(in_13), ._7D(in_14),
    ._8D(in_15), .out_12(n8_bit_register_14_out_12), .out_13(n8_bit_register_14_out_13),
    .out_16(n8_bit_register_14_out_16), .out_17(n8_bit_register_14_out_17),
    .out_18(n8_bit_register_14_out_18), .out_19(n8_bit_register_14_out_19), .in_11(or_27_out),
    .out_15(n8_bit_register_14_out_15), .out_14(n8_bit_register_14_out_14), .in_1(CLK));
  assign _1Q = not_37_out ? n8_bit_register_14_out_12 : 1'bz;  // Controlled_Buffer controlled_buffer_113
  assign _2Q = not_37_out ? n8_bit_register_14_out_13 : 1'bz;  // Controlled_Buffer controlled_buffer_114
  assign _3Q = not_37_out ? n8_bit_register_14_out_14 : 1'bz;  // Controlled_Buffer controlled_buffer_115
  assign _4Q = not_37_out ? n8_bit_register_14_out_15 : 1'bz;  // Controlled_Buffer controlled_buffer_116
  assign _5Q = not_37_out ? n8_bit_register_14_out_16 : 1'bz;  // Controlled_Buffer controlled_buffer_117
  assign _6Q = not_37_out ? n8_bit_register_14_out_17 : 1'bz;  // Controlled_Buffer controlled_buffer_118
  assign _7Q = not_37_out ? n8_bit_register_14_out_18 : 1'bz;  // Controlled_Buffer controlled_buffer_119
  assign _8Q = not_37_out ? n8_bit_register_14_out_19 : 1'bz;  // Controlled_Buffer controlled_buffer_120
  not not_37 (not_37_out, S7);
  or or_27 (or_27_out, in_7, S7);
  assign _1Q = not_38_out ? n8_bit_register_15_out_12 : 1'bz;  // Controlled_Buffer controlled_buffer_121
  _8_BIT_REGISTER u_8_bit_register_15 (
    .LOAD_prime(S11), ._1D(in_8), ._2D(in_9), ._3D(in_10), ._4D(in_11), ._5D(in_12), ._6D(in_13),
    ._7D(in_14), ._8D(in_15), .out_12(n8_bit_register_15_out_12), .out_13(n8_bit_register_15_out_13),
    .out_16(n8_bit_register_15_out_16), .out_17(n8_bit_register_15_out_17),
    .out_18(n8_bit_register_15_out_18), .out_19(n8_bit_register_15_out_19), .in_11(or_28_out),
    .out_15(n8_bit_register_15_out_15), .out_14(n8_bit_register_15_out_14), .in_1(CLK));
  assign _2Q = not_38_out ? n8_bit_register_15_out_13 : 1'bz;  // Controlled_Buffer controlled_buffer_122
  assign _3Q = not_38_out ? n8_bit_register_15_out_14 : 1'bz;  // Controlled_Buffer controlled_buffer_123
  assign _4Q = not_38_out ? n8_bit_register_15_out_15 : 1'bz;  // Controlled_Buffer controlled_buffer_124
  assign _5Q = not_38_out ? n8_bit_register_15_out_16 : 1'bz;  // Controlled_Buffer controlled_buffer_125
  assign _6Q = not_38_out ? n8_bit_register_15_out_17 : 1'bz;  // Controlled_Buffer controlled_buffer_126
  assign _7Q = not_38_out ? n8_bit_register_15_out_18 : 1'bz;  // Controlled_Buffer controlled_buffer_127
  assign _8Q = not_38_out ? n8_bit_register_15_out_19 : 1'bz;  // Controlled_Buffer controlled_buffer_128
  not not_38 (not_38_out, S11);
  or or_28 (or_28_out, in_7, S11);
  assign _1Q = not_39_out ? n8_bit_register_16_out_12 : 1'bz;  // Controlled_Buffer controlled_buffer_129
  _8_BIT_REGISTER u_8_bit_register_16 (
    .LOAD_prime(S15), ._1D(in_8), ._2D(in_9), ._3D(in_10), ._4D(in_11), ._5D(in_12), ._6D(in_13),
    ._7D(in_14), ._8D(in_15), .out_12(n8_bit_register_16_out_12), .out_13(n8_bit_register_16_out_13),
    .out_16(n8_bit_register_16_out_16), .out_17(n8_bit_register_16_out_17),
    .out_18(n8_bit_register_16_out_18), .out_19(n8_bit_register_16_out_19), .in_11(or_29_out),
    .out_15(n8_bit_register_16_out_15), .out_14(n8_bit_register_16_out_14), .in_1(CLK));
  assign _2Q = not_39_out ? n8_bit_register_16_out_13 : 1'bz;  // Controlled_Buffer controlled_buffer_130
  assign _3Q = not_39_out ? n8_bit_register_16_out_14 : 1'bz;  // Controlled_Buffer controlled_buffer_131
  assign _4Q = not_39_out ? n8_bit_register_16_out_15 : 1'bz;  // Controlled_Buffer controlled_buffer_132
  assign _5Q = not_39_out ? n8_bit_register_16_out_16 : 1'bz;  // Controlled_Buffer controlled_buffer_133
  assign _6Q = not_39_out ? n8_bit_register_16_out_17 : 1'bz;  // Controlled_Buffer controlled_buffer_134
  assign _7Q = not_39_out ? n8_bit_register_16_out_18 : 1'bz;  // Controlled_Buffer controlled_buffer_135
  assign _8Q = not_39_out ? n8_bit_register_16_out_19 : 1'bz;  // Controlled_Buffer controlled_buffer_136
  not not_39 (not_39_out, S15);
  or or_29 (or_29_out, in_7, S15);

  // Other names for the same wires on the sheet: _1D = in_8; _2D = in_9; _3D = in_10; _4D = in_11; _5D = in_12;
  //   _6D = in_13; _7D = in_14; _8D = in_15; A0 = in_6; A1 = in_5; A2 = in_2; A3 = in_1; CLR_prime = in_7;
  //   CS_prime = in_3; WE_prime = in_4
endmodule

module RAM_WITH_OUTPUT_BUFFER (
  input  in_1,
  input  in_2,
  input  in_3,
  input  in_4,
  input  in_5,
  input  in_6,
  input  in_7,
  input  in_8,
  input  in_9,
  input  in_10,
  input  in_11,
  input  in_12,
  input  in_13,
  input  in_14,
  input  in_15,
  input  in_16,
  input  in_17,
  input  in_18,
  input  in_19,
  input  in_20,
  input  in_21,
  input  in_22,
  input  in_23,
  input  in_24,
  input  in_25,
  input  in_26,
  input  in_27,
  input  in_28,
  input  in_29,
  input  in_30,
  input  in_31,
  output out_32,
  output out_33,
  output out_34,
  output out_35,
  output out_36,
  output out_37,
  output out_38,
  output out_39,
  output out_40,
  output out_41,
  output out_42,
  output out_43,
  output out_44,
  output out_45,
  output out_46,
  output out_47
);

  wire A0, A1, A2, A3, B0, B1, B2, B3, B4, B5, B6, B7, button_2_out, CLK, n4_bit_register_1_p3,
       n4_bit_register_1_p4, n4_bit_register_1_p5, n4_bit_register_1_p6, nand_1_out, not_1_out, not_2_out,
       not_3_out, R1, R2, R3, R4, R5, R6, R7, R8, WE_Control, WE_prime;

  // _4_bit_register 4_bit_register_1: pin names not known; wires that end beside it: in_29, in_30, n4_bit_register_1_p3, n4_bit_register_1_p4, n4_bit_register_1_p5, n4_bit_register_1_p6
  not not_1 (not_1_out, in_31);
  _74158 u_74158_1 (
    .in_1(n4_bit_register_1_p3), .in_2(in_20), .in_4(n4_bit_register_1_p4), .in_3(n4_bit_register_1_p6),
    .in_5(in_21), .in_6(in_23), .in_7(n4_bit_register_1_p5), .in_8(in_22), .in_9(in_31), .out_10(A3),
    .out_11(A2), .out_12(A0), .out_13(A1));
  LED led_1 (.in(in_31));
  LED led_2 (.in(not_1_out));
  SRAM sram_1 (
    .in_1(in_1), .in_2(in_2), .in_3(in_25), .in_4(in_26), .in_5(in_3), .in_6(in_4), .in_7(in_27),
    .in_8(in_5), .in_9(in_6), .in_10(in_15), .in_11(in_16), .in_12(in_17), .in_13(in_18), .in_14(in_19),
    .in_15(in_24), .out_16(out_40), .out_17(out_41), .out_18(out_42), .out_19(out_43), .out_20(out_44),
    .out_21(out_45), .out_22(out_46), .out_23(out_47));
  assign out_32 = not_2_out ? out_40 : 1'bz;  // Controlled_Buffer controlled_buffer_1
  assign out_33 = not_2_out ? out_41 : 1'bz;  // Controlled_Buffer controlled_buffer_2
  assign out_34 = not_2_out ? out_42 : 1'bz;  // Controlled_Buffer controlled_buffer_3
  assign out_35 = not_2_out ? out_43 : 1'bz;  // Controlled_Buffer controlled_buffer_4
  assign out_36 = not_2_out ? out_44 : 1'bz;  // Controlled_Buffer controlled_buffer_5
  assign out_37 = not_2_out ? out_45 : 1'bz;  // Controlled_Buffer controlled_buffer_6
  assign out_38 = not_2_out ? out_46 : 1'bz;  // Controlled_Buffer controlled_buffer_7
  assign out_39 = not_2_out ? out_47 : 1'bz;  // Controlled_Buffer controlled_buffer_8
  not not_2 (not_2_out, in_28);
  _74158 u_74158_2 (
    .in_1(B7), .in_2(in_7), .in_4(B6), .in_3(B4), .in_5(in_8), .in_6(in_10), .in_7(B5), .in_8(in_9),
    .in_9(in_31), .out_10(R1), .out_11(R2), .out_12(R4), .out_13(R3));
  _74158 u_74158_3 (
    .in_1(B3), .in_2(in_11), .in_4(B2), .in_3(B0), .in_5(in_12), .in_6(in_14), .in_7(B1), .in_8(in_13),
    .in_9(in_31), .out_10(R5), .out_11(R6), .out_12(R8), .out_13(R7));
  Button button_1 (.out(WE_Control));
  nand nand_1 (nand_1_out, CLK, WE_Control);
  _74158 u_74158_4 (
    .in_1(nand_1_out), .in_2(not_3_out), .in_9(in_31), .out_10(WE_prime));  // open: in_4, in_3, in_5, in_6, in_7, in_8, out_11, out_12, out_13
  Button button_2 (.out(button_2_out));
  not not_3 (not_3_out, button_2_out);

  // Other names for the same wires on the sheet: _1A = in_20; _1R = in_7; _2A = in_21; _2R = in_8; _3A = in_22;
  //   _3R = in_9; _4A = in_23; _4R = in_10; _5R = in_11; _6R = in_12; _7R = in_13; _8R = in_14; S_R_prime = in_31

  // Notes on the sheet:
  //   MAR
  //   My RAM  had issues so I switched to logisim's inbuil ram
endmodule

module _74158 (
  input  in_1,
  input  in_2,
  input  in_3,
  input  in_4,
  input  in_5,
  input  in_6,
  input  in_7,
  input  in_8,
  input  in_9,
  output out_10,
  output out_11,
  output out_12,
  output out_13
);

  wire and_1_out, and_2_out, and_3_out, and_4_out, and_5_out, and_6_out, and_7_out, and_8_out, not_1_out;

  Pull_Resistor #(.pull(1)) pull_resistor_1 (.node(in_1));
  Pull_Resistor #(.pull(1)) pull_resistor_2 (.node(in_2));
  Pull_Resistor #(.pull(1)) pull_resistor_3 (.node(in_4));
  Pull_Resistor #(.pull(1)) pull_resistor_4 (.node(in_5));
  Pull_Resistor #(.pull(1)) pull_resistor_5 (.node(in_7));
  Pull_Resistor #(.pull(1)) pull_resistor_6 (.node(in_8));
  not not_1 (not_1_out, in_9);
  and and_1 (and_1_out, in_1, in_9);
  and and_2 (and_2_out, not_1_out, in_2);
  and and_3 (and_3_out, in_4, in_9);
  and and_4 (and_4_out, not_1_out, in_5);
  and and_5 (and_5_out, in_7, in_9);
  and and_6 (and_6_out, not_1_out, in_8);
  or or_1 (out_10, and_1_out, and_2_out);
  or or_2 (out_11, and_3_out, and_4_out);
  or or_3 (out_13, and_5_out, and_6_out);
  Pull_Resistor #(.pull(1)) pull_resistor_7 (.node(in_3));
  Pull_Resistor #(.pull(1)) pull_resistor_8 (.node(in_6));
  and and_7 (and_7_out, in_3, in_9);
  and and_8 (and_8_out, not_1_out, in_6);
  or or_4 (out_12, and_7_out, and_8_out);
endmodule

module _4_bit_register (
  input  in_1,
  input  LOAD_prime,
  input  [3:0] in_3,
  input  in_4,
  output [3:0] out_5
);

  Pull_Resistor #(.pull(1)) pull_resistor_1 (.node(in_3[0]));
  D_FF_WITH_LOAD d_ff_with_load_1 (.in_1(in_1), .in_3(in_3[0]), .in_4(in_4), .in_2(LOAD_prime), .out_5(out_5[0]));
  Pull_Resistor #(.pull(1)) pull_resistor_2 (.node(in_3[1]));
  D_FF_WITH_LOAD d_ff_with_load_2 (.in_1(in_1), .in_3(in_3[1]), .in_4(in_4), .in_2(LOAD_prime), .out_5(out_5[1]));
  D_FF_WITH_LOAD d_ff_with_load_3 (.in_1(in_1), .in_3(in_3[2]), .in_4(in_4), .in_2(LOAD_prime), .out_5(out_5[2]));
  Pull_Resistor #(.pull(1)) pull_resistor_3 (.node(in_3[2]));
  Pull_Resistor #(.pull(1)) pull_resistor_4 (.node(in_3[3]));
  D_FF_WITH_LOAD d_ff_with_load_4 (.in_1(in_1), .in_3(in_3[3]), .in_4(in_4), .in_2(LOAD_prime), .out_5(out_5[3]));
endmodule

module PC (
  input  Clear,
  input  CLK,
  input  in_3,
  input  in_4,
  input  in_5,
  input  in_6,
  input  CE,
  input  CO,
  input  Load,
  output out_10,
  output out_11,
  output out_12,
  output out_13,
  output D0,
  output D1,
  output D2,
  output D3,
  output out_18,
  output out_19,
  output out_20,
  output out_21
);

  wire not_1_out;

  Pull_Resistor #(.pull(1)) pull_resistor_1 (.node(in_4));
  Pull_Resistor #(.pull(1)) pull_resistor_2 (.node(in_3));
  Pull_Resistor #(.pull(1)) pull_resistor_3 (.node(in_6));
  Pull_Resistor #(.pull(1)) pull_resistor_4 (.node(in_5));
  not not_1 (not_1_out, CO);
  _74161 u_74161_1 (
    ._1__nMR(Clear), ._2__CP(CLK), ._3__D0(in_3), ._4__D1(in_4), ._5__D2(in_5), ._6__D3(in_6), ._7__CEP(CE),
    ._14__Q0(out_21), ._13__Q1(out_20), ._12__Q2(out_19), ._11__O3(out_18), ._10__CET(CE), ._9__nPE(Load));  // open: _8__GND, _16__Vcc, _15__TC
  assign out_10 = not_1_out ? 1'b0 : 1'bz;  // Controlled_Buffer controlled_buffer_1
  assign out_11 = not_1_out ? 1'b0 : 1'bz;  // Controlled_Buffer controlled_buffer_2
  assign out_12 = not_1_out ? 1'b0 : 1'bz;  // Controlled_Buffer controlled_buffer_3
  assign out_13 = not_1_out ? 1'b0 : 1'bz;  // Controlled_Buffer controlled_buffer_4
  assign D0 = not_1_out ? out_21 : 1'bz;  // Controlled_Buffer controlled_buffer_5
  assign D1 = not_1_out ? out_20 : 1'bz;  // Controlled_Buffer controlled_buffer_6
  assign D2 = not_1_out ? out_19 : 1'bz;  // Controlled_Buffer controlled_buffer_7
  assign D3 = not_1_out ? out_18 : 1'bz;  // Controlled_Buffer controlled_buffer_8
endmodule

module _7_segment (
  input  in_1,
  input  in_2,
  input  in_3,
  input  in_4,
  input  in_5,
  input  in_6,
  input  in_7,
  input  in_8
);

  wire [3:0] ram_1_data_2, ram_1_data_4;
  wire [6:0] ram_1_data_3;
  wire [14:0] ram_1_data;

  _7_Segment_Display u_7_segment_display_1 (
    .g(ram_1_data_3[0]), .f(ram_1_data_3[1]), .a(ram_1_data_3[6]), .b(ram_1_data_3[5]), .e(ram_1_data_4[0]),
    .d(ram_1_data_4[1]), .c(ram_1_data_4[2]), .dp(ram_1_data_4[3]));
  _7_Segment_Display u_7_segment_display_2 (
    .g(ram_1_data[8]), .f(ram_1_data[9]), .a(ram_1_data[14]), .b(ram_1_data[13]), .e(ram_1_data_2[0]),
    .d(ram_1_data_2[1]), .c(ram_1_data_2[2]), .dp(ram_1_data_2[3]));
  RAM #(.dataWidth(24), .bus("asynch")) ram_1 (
    .addr({in_8, in_7, in_6, in_5, in_4, in_3, in_2, in_1}),
    .data({ram_1_data_4[3], ram_1_data_3[6:5], ram_1_data_4[2:0], ram_1_data_3[1:0], ram_1_data_2[3], ram_1_data[14:13], ram_1_data_2[2:0], ram_1_data[9:0]}));  // open: sel, ld, clr
  _7_Segment_Display u_7_segment_display_3 (
    .g(ram_1_data[0]), .f(ram_1_data[1]), .a(ram_1_data[6]), .b(ram_1_data[5]), .e(ram_1_data[2]),
    .d(ram_1_data[3]), .c(ram_1_data[4]), .dp(ram_1_data[7]));
endmodule

module Ram_module (
  input  [7:0] BUS_data,
  input  [7:0] SW_data,
  input  [3:0] BUS_add,
  input  [3:0] SW_add,
  input  in_5,
  input  R0,
  input  Clear,
  input  R0_2,
  input  CLK,
  input  WR_prime,
  input  pwr,
  output [7:0] out_12,
  output run,
  output [7:0] out_14,
  output Program
);

  wire and_1_out, and_2_out, and_3_out, d_ff_1_q, not_2_out, not_3_out, or_1_out;
  wire [3:0] multiplexer_2_out;
  wire [7:0] multiplexer_1_out;

  not not_1 (Program, in_5);
  not not_2 (not_2_out, in_5);
  and and_1 (and_1_out, CLK, pwr);
  Multiplexer #(.width(8)) multiplexer_1 (
    .in0(BUS_data), .in1(SW_data), .out(multiplexer_1_out), .sel(in_5));  // open: en
  Multiplexer #(.width(4)) multiplexer_2 (
    .in0(BUS_add), .in1(SW_add), .out(multiplexer_2_out), .sel(in_5));  // open: en
  not not_3 (not_3_out, WR_prime);
  D_Flip_Flop #(.trigger("high")) d_ff_1 (.clk(CLK), .D(and_1_out), .Q(d_ff_1_q));  // open: Qn, preset, en, reset
  and and_2 (and_2_out, not_3_out, in_5);
  and and_3 (and_3_out, not_2_out, d_ff_1_q);
  or or_1 (or_1_out, and_2_out, and_3_out);
  RAM #(.addrWidth(4), .bus("separate")) ram_1 (
    .addr(multiplexer_2_out), .din(multiplexer_1_out), .data(out_12), .str(or_1_out), .clk(CLK), .ld(R0),
    .clr(Clear));  // open: sel
  assign out_14 = R0_2 ? out_12 : 8'bz;  // Controlled_Buffer controlled_buffer_1

  assign run = in_5;

  // Other names for the same wires on the sheet: P_R_prime = in_5

  // Notes on the sheet:
  //   0- RUN
  //   1- Program
  //   WR' is switch button to load the data
  //   PWR is control signal for run mode, when it is one data loaded into register
endmodule
